// Logisim project grDeltaMem.circ as structural Verilog: 1 circuit, main circuit grnDeltaMem
module grnDeltaMem (
  input  [6:0] in_1,
  output [23:0] out_2
);

  ROM #(.addrWidth(7), .dataWidth(24)) rom_1 (.addr(in_1), .data(out_2));  // open: sel

  // Notes on the sheet:
  //   contents of rom_1 (hex, n*v repeats v):
  //   3d01f 5c020 7c020 9c022 be021 df020 ff020 11f020 13f006 14501e 16301d 18001e 19e01e 1bc01d 1d901e
  //   1f701d 21401e 23201e 25001e 26e01e 28c01e 2aa01d 2c701e 2e501e 30301e 32101e 33f01e 35d01e 37b01e
  //   39901e 3b701e 3d501e 3f301e 41101e 42f01e 44d01e 46b01e 48901e 4a701c 4c301b 4de01c 4fa01f 51901e
  //   53701c 55301d 57001b 58b01e 5a901f 5c801f 5e7020 60701e 62501f 64401e 66201f 681020 6a1020 6c101f
  //   6e001d 6fd01f 1e 1e01f b134e8 73f023 762023 785023 7a8023 7cb023 7ee023 811023 834023 857023 87a023
  //   89d023 8c0023 8e3023 906023 929023 94c023 96f023 992023 9b5023 9d8023 9fb023 a1e023 a41023 a64023
  //   a87023 aaa023 acd023 af0023 b134e8
endmodule
