// Logisim project grnMem2.circ as structural Verilog: 1 circuit, main circuit grnMem2
module grnMem2 (
  input  [6:0] in_1,
  output [31:0] out_2
);

  ROM #(.addrWidth(7), .dataWidth(32)) rom_1 (.addr(in_1), .data(out_2));  // open: sel

  // Notes on the sheet:
  //   contents of rom_1 (hex, n*v repeats v):
  //   204e821 204e822 204e823 204e824 204e825 204e826 204e827 204e828 204e863 a04e821 a04e822 a04e823
  //   a04e824 a04e825 a04e826 a04e827 a04e828 a04e829 a04e860 a04e861 a04e862 a04e863 a04e864 a04e865
  //   a04e866 a04e867 a04e868 a04e869 a04e8a0 a04e8a1 a04e8a2 a04e8a3 a04e8a4 a04e8a5 a04e8a6 a04e8a7
  //   a04e8a8 a04e8a9 a04e8e0 a04e8e1 a04e8e2 a04e8e3 a04e8e4 a04e8e5 c04e821 c04e822 d04e821 d04e822
  //   d04e823 d04e824 d04e825 d04e826 d04e827 d04e828 d04e829 d04e860 d04e861 d04e862 d04e863 8004e821
  //   8004e822 700f011 904cf9a3 904cf9a4 904cf9a5 904cf9a6 904cf9a7 904cf9a8 904cf9a9 904cf9e0 904cf9e1
  //   904cf9e2 904cf9e3 904cf9e4 904cf9e5 904cf9e6 904cf9e7 904cf9e8 904cf9e9 904cfa20 904cfa21 904cfa22
  //   904cfa23 904cfa24 904cfa25 904cfa26 904cfa27 904cfa28 904cfa29 904cfa60 700f011
endmodule
