// Logisim project proverka21.circ as structural Verilog: 1 circuit, main circuit proverkaChip21
module proverkaChip21 (
  input  C,
  input  in_2,
  input  [11:0] in_3,
  output [3:0] out_4,
  output out_5,
  output [15:0] out_6,
  output [15:0] out_7
);

  wire and_1_out, and_2_out, counter_1_carry, d_ff_1_q, d_ff_1_qn, not_1_out;
  wire [15:0] controlled_buffer_1_out, shift_register_1_q0;

  Counter #(.width(4), .max('hf), .ongoal("stay")) counter_1 (
    .count(C), .Q(out_4), .carry(counter_1_carry), .clk(C));  // open: load, D, clr
  not not_1 (not_1_out, C);
  and and_1 (and_1_out, counter_1_carry, not_1_out);
  D_Flip_Flop d_ff_1 (.clk(C), .D(and_1_out), .Q(d_ff_1_q), .Qn(d_ff_1_qn));  // open: preset, en, reset
  and and_2 (and_2_out, d_ff_1_qn, C);
  ROM #(.addrWidth(12), .dataWidth(16)) rom_1 (.addr(in_3), .data(out_6));  // open: sel
  Shift_Register #(.length(16)) shift_register_1 (
    .shift(1'b1), .in(in_2), .clk(and_2_out), .q0(shift_register_1_q0[0]), .q1(shift_register_1_q0[1]),
    .q2(shift_register_1_q0[2]), .q3(shift_register_1_q0[3]), .q4(shift_register_1_q0[4]),
    .q5(shift_register_1_q0[5]), .q6(shift_register_1_q0[6]), .q7(shift_register_1_q0[7]),
    .q8(shift_register_1_q0[8]), .q9(shift_register_1_q0[9]), .q10(shift_register_1_q0[10]),
    .q11(shift_register_1_q0[11]), .q12(shift_register_1_q0[12]), .q13(shift_register_1_q0[13]),
    .q14(shift_register_1_q0[14]), .q15(shift_register_1_q0[15]));  // open: out, load, clr, d0, d1, d2, d3, d4, d5, d6, d7, d8, d9, d10, d11, d12, d13, d14, d15
  assign controlled_buffer_1_out = d_ff_1_q ? out_6 : 16'bz;  // Controlled_Buffer controlled_buffer_1
  Comparator #(.width(16)) comparator_1 (
    .a(controlled_buffer_1_out), .b(shift_register_1_q0), .eq(out_5));  // open: gt, lt
  assign out_7 = shift_register_1_q0 ^ controlled_buffer_1_out;  // XOR_Gate xor_1, 16 bits wide

  // Notes on the sheet:
  //   Вход логической функции
  //    (Номер варианта - 1) как двоичное 10ти разрядное число
  //   contents of rom_1 (hex, n*v repeats v):
  //   d66b 9eba 5a3f 79f1 7e5c 35fc ac5f cf9a bd5a 9d3b 97cd 7597 bcb3 b9ab f87a 3f5a ac9f c65f ff18 70bf
  //   fd83 b739 734f 74fa e679 ee0f d79a f2c7 97ce edc3 6f9a b99b c76b ed17 69af ed5c 93cf fd2a 987f ba97
  //   bbac b567 794f e2fa eaa7 f8ab acee fb23 e9e5 e72e 5fd1 6f1d fc96 ea7c a5d7 673d 9dda f07d 79ae aead
  //   b4fc ebaa f0f5 7b8e b7f f574 2b5f dc7c 4edb 8bd7 17ee 2a7f a7ab d9da c737 dec9 7c4f e55e f3a9 ced9
  //   37cb 16fd 5cf6 d95b 53d7 6fd8 e9d5 5abe fe64 fe45 8be7 cf74 f734 ebc5 ba6e f1ce 1cbf 6ade a39f fc3a
  //   ff06 d2bb 6d9b bcd6 4bfa f9e8 536f 9cd7 da79 bec5 f8e5 fad8 db96 7c6b adf1 c4f7 713f 779a e8be d33b
  //   e0bf b71e e79c 5fcc 7a7a 4d7d c3cf b637 67f2 e35d e36e e4db cbf8 e4be bdca ea3b afcc db71 75ad 53fa
  //   fb92 f70b 86bf cddc f8e9 cf17 5fe4 de8b 57cb 7af1 6eb6 abae 7d56 1f2f 8e77 d6f1 de59 f5c9 ed47 dd2b
  //   eca7 deca 2b7d 7575 15fd fdd cbce 7769 ef54 f7a2 7ad6 d756 df32 d71b d573 a9eb eacd 15f7 6773 693f
  //   f93a fda1 d59b 9df4 fb38 3b1f e55b 7e1b ede4 bb9c af6c ec9d daf8 ab57 12ff 9f8b 49bf 6d76 4cfd 55eb
  //   acbd dd78 f876 8d7d d3c7 4fb5 cbcd 7d2d f972 e4dd 7c3d b66e f743 687f 9f53 3f66 74dd fe89 d37c fb70
  //   e5cb 7ad5 d3ad cfe1 bae9 9acf ce73 9f63 1cf7 eb5c d6e3 b62f f64e 7d17 fad4 76cd 2eb7 fc99 9776 8dfc
  //   1bee a3ed 3d9b 9eb3 1fdc 672f aae7 d5ba 5bb6 8e7e ed1b 1ef9 dd36 1fb5 357d def0 5fc9 cbbc 1b9f f94d
  //   43ef e53d cabd 2fcb 3a77 a37b fe86 5be3 a3bb 3f63 b736 d9dc 7eca 6d73 f237 a7ce a76e 39fa dda9 6f59
  //   6ccf 90ff 9b8f bfc2 7d2e 7cce b1dd 6bb9 b7d8 decc f8f2 37d6 b8bb 33b7 cd7a 73dc 7a9d f7c8 3f72 f273
  //   f6c6 ef46 db35 b5d3 d93e 1ef6 f1e3 27f9 fbb0 e8f5 637d da8f 77b4 72db 559f 3f8b b79a c3af dcf1 ab9d
  //   65b7 eac7 aeb3 ddc6 d747 8bf5 399f 7766 5f9c f3e2 53ed c1ef 9db6 d5f4 d43f f785 7b74 f56a bab3 4bf5
  //   7d1d dba5 2fd3 b74e 956f 1e7d 39f5 9e7c b95b 7ee2 f5aa f3ca 1fc7 adf8 bf45 cabe 3b9e a7e9 e67c 9f5a
  //   3f35 f363 49fb e92f cf87 5f59 dc76 83fd e3da d575 ef8c 1f57 fab1 6ef8 d91f f0e7 cf99 1d7b dc9b be1d
  //   3a7b 1fcd dd4d 5bad 7f4a 7ec9 6b5d 4efc d4ed b1bd 6767 6ece ba1f 9e76 ac6f ecf1 d9f2 7e53 566f fc55
  //   7a4f d8bb 63f5 6b6e bc3b dd1e 17b7 c5bd fab8 c775 9caf 67b6 b3f4 d1be 3f1b b56d ba73 7b39 676e 73c7
  //   af27 d795 4edd 37bc cf56 edb2 ad79 f3f0 7be1 8fae 792f e9e9 8f4f 76d5 f39a ed72 b5cd 5b9e a5ee c7a7
  //   fbe 9abb 25fb c56f 66be aff bb39 89df 93db 2ff8 c6e7 7f46 5de5 baf1 f723 b4e7 16fb f1d3 4b7b a9d7
  //   ef58 bc37 7bd4 eae5 7e3a d57c cfa3 dc6d 778d 9cbb 54df fe25 e75a 9d4f a4bf ad67 b8f9 c9eb 674f bd4b
  //   a79b 92fd 7f07 9d6e f9d8 27be f91e d7d4 dcd9 59dd fc71 bc6b efb0 baae f38b e15f f87c 77a9 5be6 6ed5
  //   6f65 cbd5 df07 966f 5bdc d6ab 7eac 9e37 9bd3 f19e 87de 5d2f 52fb 4ecf db4d d7b4 6775 ceb6 de53 376e
  //   bbaa f366 7e71 7ee1 a577 b799 af2e f9a5 2fda 95fa 2c7f 2fe3 74e7 de87 dad3 6bb6 fc78 578f d9e3 5fb1
  //   ae2f 4bb7 6b73 d7c3 f3aa 751f b6dc de5a 17ed a6af aeb9 e4f5 e56e ef51 ec73 a6fc 796d f89e bf64 a1bf
  //   35e7 dbb8 5dce 3fc5 55b7 f176 38bf 1de7 bb1b a737 8ff4 df8c ad97 57f2 3add 9aaf a977 af47 6c77 bb4e
  //   5eba 37e9 7cad e7ac ecc7 1d9f 7e39 29bf 74f9 377c fe07 55dd 4f9b aee9 8fba 7b47 e45f 79f4 f5e8 cbf1
  //   ee56 e73c 5dd6 4cdf cd3d fd51 c63f dae6 bcdc 96d7 dc4f 2eaf b36d fc1d adad afb2 e765 a3be 7a5b faf
  //   8f6b dcb9 b1f5 e771 317f cd3b b1f3 cf8e eb1b 5f4d cfc9 f35c b91f cb6b b8fa e96e e5e3 6f2d ef52 f30f
  //   9bf4 7e47 d8b7 5fa3 da2f ae75 ff09 d0fd b39d 8f1f 6cbd fc2e af2d 37b3 69f5 6e67 d967 99af 7d6c 7bac
  //   dd5a f8d6 9f99 24ff 77aa ee8d f5cc 9ebc f64d 2bed f25b 7b66 857f e6a7 7397 93b7 ee39 d9e9 be3c f0fc
  //   bfe 776a b4f5 b9cb aed5 5ef8 6c7e 479f ec9b b55d 7f26 cd9b 5ef2 d697 e5a7 29df ade6 d8dd a7e5 f5d1
  //   d7e8 f51b 3977 7e0f 7739 9eab e47b fb86 f66a 46fb af71 3be9 d1ed 3577 dfd 13fe b87d 75d5 d4f9 f59a
  //   5d67 b3ae 6ea7 bb2d bca7 7e65 dad5 746f d5e6 c3de bace 6b2f 9f59 33f9 f917 1fe3 7ea3 1eee 8bcf becc
  //   7ee4 8b5f 2f1f f6e8 3ed3 e739 eec6 eeb1 6f27 78ee ecbc dfa4 367d 635f 1bf9 ff14 cf71 f8ae f9ca adae
  //   5fe1 76ce 6add 69b7 ba6b 25fe e1f3 74cf dadc c6f9 73b9 dfa8 f7c2 bdc3 6d5d c67e 9ccf cbe5 fc5c df31
  //   1df9 daab 3d5e 69e7 7ec3 23ef 5f78 cb5e dc5d 9ddc ffc ef13 7772 adda 4f67 e91f a7ae 7e6c 33eb 793d
  //   27b7 bf0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
  //   Входной набор для функции со счетчика
  //   Результат оценки 1 - правильно
  //   Диагностика ошибок
endmodule
