// Logisim project stnMem1.circ as structural Verilog: 1 circuit, main circuit stnMem1
module stnMem1 (
  input  [11:0] in_1,
  output [31:0] out_2
);

  ROM #(.addrWidth(12), .dataWidth(32)) rom_1 (.addr(in_1), .data(out_2));  // open: sel

  // Notes on the sheet:
  //   contents of rom_1 (hex, n*v repeats v):
  //   b2cb0035 b2cb2cb0 b2cb0100 b2cb2c04 b2cb2c04 b2cb0201 b2cb2cb2 b2c0d020 b2cb2c28 b2cb2cb0 b2cb2cb0
  //   b2cb2cb2 b2cb2cb2 b2cb0c15 b2cb2c30 b2cb2cb0 b2cb2c34 b2cb2c3c b2cb2cb0 b2cb2c3c b2cb2cb2 b2cb2c3d
  //   b2c44010 b2cb2cb1 b2cb1100 b2cb2cb1 b2cb2cb1 b2cb2c44 b2cb2cb2 b2cb2cb2 b0045201 b2cb0055 b2cb2c04
  //   b2cb2c08 b2cb2c08 b2cb2cb0 b044c138 b2cb2cb2 b2cb2cb2 b2c2802c b2cb2c28 b2cb2cb2 b2cb2cb2 b2cb2cb2
  //   b2cb0c00 b2cb2cb0 b2cb0f01 b2cb2cb2 b2cb2cb2 b2cb2c3d b2cb2cb2 b2cb2cb2 b2cb2c40 b2cb2c40 b2cb2cb2
  //   b2cb1114 b2c44a01 b2cb2c45 4*b2cb2cb2 b0418034 b2cb2c10 b2c11330 b0700d14 b2cb2cb2 b2cb2c21 b2cb2cb2
  //   b2cb2cb2 b2c28e34 b2c28e34 b2cb2cb2 b2cb2cb0 b2cb2cb2 b2cb2cb2 b2cb0c14 b2cb0c21 b2cb0d00 b2cb2cb0
  //   b2cb1038 b2cb2cb1 b2cb1100 b2c45201 b2cb114d b2cb2c50 b2cb2cb1 b2cb2cb1 b2c55000 b2cb2cb1 b2cb1915
  //   b2cb2cb2 b2cb2cb2 b2cb2cb0 b2cb2cb0 b0138301 b2cb2c04 4*b2cb2cb2 b2cb2cb0 b2cb2cb0 b2cb2cb0 b2cb2c1c
  //   b2cb2cb0 b2cb2cb2 b2cb2cb0 b2cb2cb0 b2cb2c28 b2cb2c28 b2cb2cb2 b2cb2c2d b2cb2cb2 b2cb2cb0 b2cb2cb2
  //   b2cb2cb2 b2c3ce29 b2cb2c44 b2cb1240 b2cb2cb1 b2cb2c54 b2cb2cb1 b2cb2cb2 b2cb2cb2 b2c04e34 b2cb2cb0
  //   b2cb2c08 b2c08834 b2cb2cb0 b2c0c010 b2cb2c0c b2cb2cb0 b2cb2cb0 b2cb2cb2 b2cb2cb0 b2cb2c29 b2cb2cb0
  //   b2cb2cb2 b2cb2c30 b2cb2cb0 4*b2cb2cb2 b2cb2cb1 b2cb2cb2 b2c44030 b2cb2c44 b2cb2c44 b2cb2cb1 b2cb2cb1
  //   b2cb1138 b114853c b2cb2c49 b2cb2cb2 b2c00b72 b2cb2c09 b2cb2cb2 b2cb2cb0 b2cb0414 b2cb2cb0 b2cb2cb2
  //   b2cb0a39 b2cb2cb2 b2cb0c00 b2cb2c30 b2cb2c30 b2cb2c30 b2cb0d14 b2cb2cb2 b0f38d38 b2cb2cb1 b2c44540
  //   b2cb2cb1 b1128e40 b2cb1148 b2cb2cb2 b1500c20 b2cb1714 b2cb2cb2 b2cb2cb1 b2cb2cb2 b2cb2cb2 b2cb2cb0
  //   10e05038 b2cb0a01 b2cb2c30 b2cb2cb0 b2cb2cb0 b2cb2cb2 b2cb2cb0 b2cb2cb2 b2cb2cb0 b2c0802c b2cb2cb0
  //   b2cb2cb0 b2cb2cb2 b2cb2cb0 b2cb2c1c b2cb2c1d 4*b2cb2cb0 b2cb2c34 b2cb2c3c b1100f14 b2cb2cb1 b2cb2cb1
  //   b2cb114c b2cb2cb1 b2cb2c48 b2cb2c48 b2cb2cb2 b2cb2c60 b2cb2c7c b2cb2cb2 b2cb2c00 4011000 b2cb0100
  //   b2cb2cb2 b2cb2cb2 b2cb2cb2 b2cb2cb0 b2c04511 b2cb0114 b2c05079 b2c0532c b2cb2cb2 b2cb2c0d b2cb2cb0
  //   b2cb2cb2 b2cb0700 b2cb2cb2 b2cb2cb0 b2cb2cb2 b2cb2cb0 b2cb2cb2 b2cb2cb2 b2cb2c29 b2cb2cb2 b2cb0b14
  //   b2cb2cb2 b2cb2cb0 b2cb0c01 b2cb2cb0 b2cb2cb0 b2cb0d38 b2cb1100 b2cb2cb1 b2cb1115 b2cb2cb1 b2cb2cb2
  //   b2cb1814 b2cb2cb0 b2cb2cb0 b2cb2cb2 b2cb2c04 b2cb2cb2 b2cb2cb0 b2cb0215 b2cb2c08 b2cb2c08 b2cb2c0c
  //   b2cb2cb0 b2cb2cb2 b2cb2cb0 b2cb0a38 b2cb2c28 b2cb2cb2 b2c30840 b2cb2cb2 b2cb2cb0 b2cb0c38 b2cb2cb2
  //   b2cb0d20 b2cb0d38 b2c40004 b2cb2cb2 b2cb2cb2 b2cb2c44 b1114239 4*b2cb2cb2 b2cb2cb0 b2cb2c00 b2cb2cb2
  //   b2cb2cb0 b2cb2cb2 b2cb0215 6*b2cb2cb2 b2cb0a40 b0a40530 b2cb2c29 b2cb2cb0 b2c3130c b2cb2cb2 b2cb2c34
  //   b2cb2c3c b2cb2cb2 b2c44030 b2cb2c44 b2cb2cb1 b2cb2cb1 b2cb2cb1 b2cb2cb2 b2cb1508 b2cb2cb1 b2cb2c5c
  //   b2cb2c60 b1814138 b2cb2cb0 b2cb2c11 b2cb2c3c b2cb2cb1 b2cb2cb1 b2cb2cb2 b2cb2c00 b0034441 b2cb2cb2
  //   b2cb2cb0 b2cb2c0c b2cb2c10 b2cb2cb0 b2cb082d b2cb2cb0 b2cb2c2c b2cb2cb2 b2cb2c30 b2cb2c30 4*b2cb2cb0
  //   b2c3ce3c b2cb2cb2 b2cb2cb2 b2cb2cb2 b2cb2c44 b2cb2cb1 b2cb2cb1 b2cb2cb1 b2cb1201 b2cb1815 b2cb2c60
  //   b2cb2c60 b2cb2c40 b2cb002c b2cb2c00 b2cb2c04 b2cb2c04 b2cb0315 b2cb0340 b2cb2c10 b2cb2cb0 b2cb2cb0
  //   b2cb2c19 b2cb2c28 b2cb2cb2 b2cb2cb0 b2cb2cb0 b2cb2c30 b2cb2c34 b2cb2c34 b2cb2cb0 b1000760 b2cb2cb2
  //   b1114b20 b2cb2c45 b2cb2c45 b2cb2cb2 b2cb2cb2 b2cb1701 b2cb2c5d b2cb2cb1 b2cb1914 b2cb2cb2 b2cb2cb0
  //   b2cb2cb2 b2cb2c08 b2cb2cb2 b2cb2c0d b2cb2cb0 b2cb2cb0 b2cb0441 b2c14245 b2cb2cb0 b2cb2cb2 b2cb2cb2
  //   b2cb2cb0 b2cb2cb2 b2cb2cb2 4*b2cb2cb0 b2c3c549 b2cb0f38 b0f38460 b2cb2cb2 b2cb2c44 b2cb2cb1 b2c44b15
  //   b2cb1148 b2cb1149 b2cb2cb2 b2cb2c00 b2c00d11 b2cb2cb0 b2cb2cb2 b2cb2cb2 b2c0d038 b2cb2cb0 b2c10c21
  //   b2cb0530 b2cb2cb2 b2c1c00c b2cb2c28 b2cb0a01 b2cb2cb0 b2cb2cb0 b2cb2c28 b2cb2c30 b2c30029 b2cb0c15
  //   b2cb0c21 b2c31354 b2cb2c3c b2cb2cb0 b2cb2c44 b2cb1138 b2cb2c45 b2cb2cb2 b2cb2cb1 b2cb2c7c b2cb1f45
  //   b2cb2cb0 b2cb2cb2 b2cb014c b2cb2cb0 b2cb2c0c b2cb2cb2 b2cb2c11 b2cb2cb2 b2cb2cb2 b2cb081c b2cb2cb2
  //   b2cb2cb0 b2cb2cb0 b2cb2cb0 b2cb0a4c b2cb2cb0 b2cb0c00 b2cb2cb0 b2cb2cb0 b2cb1038 b2cb2cb2 b2cb2cb2
  //   b2cb2cb1 b2cb2c49 b2cb2c5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
endmodule
