// Logisim project stnMem2.circ as structural Verilog: 1 circuit, main circuit stnMem2
module stnMem2 (
  input  [11:0] in_1,
  output [31:0] out_2
);

  ROM #(.addrWidth(12), .dataWidth(32)) rom_1 (.addr(in_1), .data(out_2));  // open: sel

  // Notes on the sheet:
  //   contents of rom_1 (hex, n*v repeats v):
  //   62141503 41520f3 a2c034e0 540518d3 540c20d3 54136050 c08e2ca3 339014d2 61200d3 a21114b1 a38200b1
  //   cb0a3923 c2c05483 91507ca3 854024b7 d14b2043 e0885ca3 535c6083 f15240e0 54904d74 cb0f38f3 38d2883
  //   e08d20a3 10060050 c01044a2 12884850 13054122 e28e2ce0 cb1420b2 c60b14f2 814244a2 33477cd3 e0c400d3
  //   4482dc1 e2ce0531 33907d71 220d44a2 cb2cb064 cb2c1d31 835720a3 b20c14d2 cb0a3971 cb0b6ca3 cb0b6d10
  //   338c1443 e2c14d23 c38d3 cb0f38f3 cb0f38f3 3953903 c3d32802 cb0f4d82 48d20a3 560548d7 c40e18a3
  //   d5c028e0 16d044a2 238b4cf2 cb1220d2 cb122123 c61330a3 cb016ca3 c2101ce1 c2124081 139f34e0 c38d44a2
  //   cb084152 130020b3 cb2cb0a2 c28e2d71 440049c1 e34548e0 cb0a4001 a4c770c3 c2c00803 c2d31c32 b71700a3
  //   500b7174 33822162 f38b7ca3 c00d14d2 100220d3 b00c0122 3844c13 12df28e0 510e40e0 421114d2 50142073
  //   c3822171 81426d01 4028e0 cb1e60a3 cb002c81 35220f3 10150101 26d070a3 e2c46d01 c0530c01 c08e2ca3
  //   c0ce4521 c1054167 41581426 551014c3 601028e0 30e4801 70150103 c20200d3 84030181 a0074c13 e2c10112
  //   e5c54032 cb2cb2c2 e05714d2 c30828e7 c21038d3 c3400481 c3c54903 38244a2 50040e0 80453442 44003561
  //   41714d2 801020a3 c7d11422 cb0114b3 401014d2 14002574 4482dc1 e0d00043 238b28e0 621500d3 e2dc58e0
  //   34d10103 414c2043 c18040e0 701020f3 31cd1563 b0070101 cb0b14d1 29120c3 c01028e0 c3085483 c3c54900
  //   c3c54903 c3d038d2 4c400a3 cb107c13 e24b14d2 31138d3 540478a3 120c38d3 138a38b3 b38c0152 34534a3
  //   318534a3 cb2c7842 a5402df0 f2dc6083 cb034d03 40093452 d21114d2 70150103 c28e40d1 14854050 cb0b7c33
  //   338c1443 40558a2 41714d2 58e2883 220420c3 cb0f38b1 c01014d2 10150103 e61200d3 120c38d3 e54e10e0
  //   8858a2 cb1148e2 44cb2c83 d2802c51 c5c540d6 809b10a2 cb1e40a3 c7ca4d81 22124d82 238b7112 34858a0
  //   34034a3 d3912103 e1083401 c00f0102 4127953 cb0114b3 200a4cb3 535220d3 341b1cb3 50ce4083 cb054183
  //   620300d3 9c7cb3 305020b2 a00d0123 b38100d3 c3903873 d0041462 828e2c01 41414d3 620d44a2 120258e0
  //   130840d3 a38b14d3 20070481 2920103 a01714d2 c4902182 40400d3 a3822c50 c0012181 210514d2 db102124
  //   b4800401 c2802c40 cb2cb170 c0070107 29114d3 14420d3 71d304a2 538244a2 e60d20a3 c0843822 2040113
  //   414c1552 c10824a4 238b38a2 c1c020a2 700b14d1 c20200d3 a00100d3 c2801081 c2906cb3 340478a3 cb0b0153
  //   338d70a3 c2d304a2 c00a2df1 23134401 c14b2153 c20a2127 238620b3 b70d20a3 114c14d3 14da8e3 14805051
  //   c4c30103 b38c00d3 29800d3 3444051 c0450cb3 540518d3 c0802c51 200b2123 4858a2 541820d2 e40e05c1
  //   b0046d81 34c100d3 c20200d3 a00700a3 f39220b3 e40004b2 c3002cd0 e60d20a3 c3084883 c38320b1 b38a00d3
  //   cb0d0072 a2143903 24131ce0 1c034e0 c40e4804 cb107c11 1c034a2 149c7cd3 c44e04e2 c5084113 c78c0181
  //   cb1e40a3 1c034e0 b7014055 c04e10d0 13903842 cb016ca3 6083483 c08e2ca3 cb0320b0 c0d04d82 cb070082
  //   c20200d3 c28b20c3 9714d2 d14244a2 340534d6 b38320d3 2c830e0 c3132c01 24414d3 3541503 cb0f38b7
  //   e54200b3 22102043 138b38f3 221538d3 40122153 c51038b3 e40e4522 72012113 84527952 28b1483 b10534a3
  //   34d044a2 310d20a3 55c534a2 10883563 800300b2 c6002906 d1054113 360a1422 cb016ca3 300b7161 524b14d2
  //   e2cc0123 720c0101 c7d814d2 a38c0103 e3c048a3 cb0b3911 4903913 854024b3 c4d00123 d4d04cb2 f00d7182
  //   f0124083 b00244a2 c41b18a3 c41b18e0 cb111443 530524a2 114c14d3 120d2166 130840d3 71422 45278a3
  //   84083411 a38b70d2 51cd20a3 834114a3 d1103913 40a00d3 e2ce48e0 1120c3 805714d2 54060022 50ce40a2
  //   610034e0 340008b1 6053561 c2906cb3 a4cb00a3 a4cb70a3 540534a3 54521503 82884883 f3903982 82dc11f1
  //   c4070050 21504523 201614d2 e30028e0 cb142c51 c5484903 138244a2 35084523 801828e0 a3922152 cb002c81
  //   100614d3 c05310a3 4482dc1 c08b0113 344524d3 414d2113 439038d2 319714d2 240048e0 540e5051 c1c21501
  //   c2022c81 a00d5d34 c2936153 cb0b3813 c00700d3 c0120851 d0111422 f15240e0 38244a2 214414d3 80802ce0
  //   c4001001 4920103 12043903 101014d2 4135483 14b28e0 c79120f3 100a4cc3 c00d3 139038d2 c0534161
  //   c08e5502 c6d500b2 40026c47 240814d2 52dc7cd3 cb0620b2 e40e10d6 1c03561 f1527 a08060d2 a38200b1
  //   e3db2ce0 29120a3 120c14d2 1cb7ca3 79914d2 3054982 e2c54801 f38b7ca3 1ce34e0 b11334e0 30413922
  //   cb120100 20100113 a3822c50 240504e0 10182103 c04b3952 b0c028e0 30041881 e41e34e0 c0d02182 304828e0
  //   cb054163 c19328e0 c0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
endmodule
